# Fritzing sketch datalogger (saved by Fritzing 0.9.3b)
circuit board: 8.71291cm x 5.64671cm
breadboards: 1

parts:
  Power_plug1 = Power plug
  RESET = Pushbutton [package="[THT]"]
  R1 = Resistor [tolerance=±5% resistance=1M package="1206 [SMD]"]
  L1 = Inductor [inductance=10nH package="1206 [SMD]"]
  Q1 = Basic FET P-Channel [package="DPak [SMD]"]
  FTDI_Friend = male pin header, 6 pins [form="♂ (male)"]
  BAT1 = Battery Holders [part_number=BK-912-ND package=battcon_20mm]
  WAKE_UP = Pushbutton [package="[THT]"]
  R2 = Resistor [tolerance=±5% resistance=10k package="1206 [SMD]"]
  C6 = Electrolytic Capacitor [capacitance=1µF package="0405 [SMD, electrolytic]"]
  OneWire = Molex Picoblade Series Header [part_number=0532610319 package=Picoblade-53261-0319]
  R4 = Resistor [tolerance=±5% resistance=4.7k package="1206 [SMD]"]
  U2 = SD_CARD_SOCKET [package=sdcard_4uconn]
  CPU = ATmega328 [package=tqfp]
  R3 = Resistor [tolerance=±5% resistance=10k package="1206 [SMD]"]
  U1 = Voltage Regulator [package=sot223]
  Part2 = SO16w [chip_label=IC package=SO(w)]
  C9 = Ceramic Capacitor [capacitance=100nF package="100 mil [THT, multilayer]"]
  C8 = Ceramic Capacitor [capacitance=100nF package="100 mil [THT, multilayer]"]
  C7 = Ceramic Capacitor [capacitance=10nF package="100 mil [THT, multilayer]"]
  C5 = Ceramic Capacitor [capacitance=100nF package="100 mil [THT, multilayer]"]
  C4 = Ceramic Capacitor [capacitance=100nF package="100 mil [THT, multilayer]"]
  Clock = male pin header, 3 pins [form="♂ (male)"]

nets:
  GND: Power_plug1.GND, RESET.Pin_3, RESET.Pin_4, FTDI_Friend.pin1, FTDI_Friend.pin2, BAT1.-, WAKE_UP.Pin_1, WAKE_UP.Pin_2, C6.-, OneWire.3, U2.SH, U2.VSS1, U2.VSS2, CPU.GND, U1.ADJ, Part2.5, Part2.6, Part2.7, Part2.8, Part2.9, Part2.10, Part2.11, Part2.12, Part2.13, C9.0, C8.0, C7.0, C4.0, Clock.pin3
  6V: Power_plug1.VCC, FTDI_Friend.pin3, U1.IN, C9.1
  RESET: RESET.Pin_1, RESET.Pin_2, R1.Pin_1, CPU.PC6(_RESET), C5.1
  3.3V: R1.Pin_0, L1.pin_0, Q1.source, R2.Pin_0, U2.VDD, CPU.VCC, CPU.AREF, R3.Pin_0, U1.OUT, Part2.2, C8.1, C7.1
  AVCC: L1.pin_1, CPU.AVCC, C4.1
  N1: Q1.Gate, CPU.PD5(T1)
  VSS Switched: Q1.drain, OneWire.1, R4.Pin_0
  N2: FTDI_Friend.pin4, CPU.PD0(RXD)
  N3: FTDI_Friend.pin5, CPU.PD1(TXD)
  N4: FTDI_Friend.pin6, C5.0
  N5: BAT1.+, C6.+, Part2.14
  INT/SQW: WAKE_UP.Pin_3, WAKE_UP.Pin_4, CPU.PC2(ADC2), Part2.3
  SCL: R2.Pin_1, CPU.PC5(ADC5_SCL), Part2.16
  DATA: OneWire.2, R4.Pin_1, CPU.PB0(ICP)
  CS: U2.CD_DAT3, CPU.PB2(SS_OC1B)
  MOSI: U2.CMD, CPU.PB3(MOSI_OC2)
  SCK: U2.CLK, CPU.PB5(SCK)
  MISO: U2.DAT0, CPU.PB4(MISO)
  N6: CPU.PB6(XTAL1_TOSC1), Clock.pin1
  N7: CPU.PB7(XTAL2_TOSC2), Clock.pin2
  SDA: CPU.PC4(ADC4_SDA), R3.Pin_1, Part2.15
  32kHz: Part2.1

notes:
  UW Datalogger, A datalogger for long term deployment. , 2
  Data logger
  https://github.com/flyhard/DataLoggerEagleCAD
